// Logisim project q3.circ as structural Verilog: 1 circuit, main circuit main
module main (
);

  wire and_1_out, and_4_out, and_10_out, and_11_out, and_13_out, and_14_out, and_15_out, and_16_out,
       and_17_out, and_18_out, and_19_out, and_20_out, and_21_out, and_22_out, and_23_out, and_24_out,
       and_25_out, and_26_out, and_35_out, and_36_out, and_37_out, and_38_out, and_39_out, and_40_out,
       and_41_out, and_42_out, and_43_out, and_44_out, and_45_out, and_46_out, and_47_out, and_48_out,
       and_49_out, and_50_out, and_59_out, and_60_out, and_61_out, and_62_out, and_63_out, and_64_out,
       and_65_out, and_66_out, and_67_out, and_68_out, and_69_out, and_70_out, and_71_out, and_72_out,
       and_73_out, and_74_out, and_83_out, and_84_out, and_85_out, and_86_out, and_87_out, and_88_out,
       and_89_out, and_90_out, and_91_out, and_92_out, and_93_out, and_94_out, and_95_out, and_96_out,
       and_97_out, and_98_out, clock_1_out, comparator_1_eq, comparator_2_eq, comparator_2_lt,
       comparator_3_eq, comparator_3_lt, comparator_4_gt, comparator_5_lt, comparator_6_lt, decoder_1_out0,
       decoder_1_out1, decoder_1_out2, decoder_1_out6, decoder_1_out7, decoder_2_p4, decoder_2_p5,
       decoder_2_p6, decoder_2_p7, decoder_2_p8, decoder_2_p9, decoder_2_p10, decoder_2_p11,
       multiplexer_2_out, multiplexer_3_out, nand_1_out, nand_2_out, nand_3_out, nand_4_out, nand_6_out,
       nand_7_out, nand_8_out, nand_10_out, nand_11_out, nand_12_out, nand_13_out, nand_14_out, nand_15_out,
       nand_16_out, nand_17_out, nand_18_out, nand_19_out, nand_20_out, nand_21_out, nand_22_out,
       nand_23_out, nand_24_out, nand_25_out, nand_27_out, nand_28_out, nand_29_out, nand_30_out,
       nand_31_out, or_2_out, undriven_10, undriven_11, undriven_12, xor_1_out, xor_2_out;
  wire [1:0] decoder_2_p3, undriven_9;
  wire [2:1] undriven_7;
  wire [4:0] multiplexer_5_out;
  wire [4:3] undriven_3, undriven_5;
  wire [4:4] undriven_6;
  wire [5:0] undriven_4;
  wire [5:3] decoder_2_p1;
  wire [9:0] undriven_8;
  wire [12:0] register_3_q;
  wire [15:0] adder_1_out, adder_2_out, and_5_out, and_6_out, and_7_out, and_8_out, and_9_out, and_12_out,
       and_27_out, and_28_out, and_29_out, and_30_out, and_31_out, and_32_out, and_33_out, and_34_out,
       and_51_out, and_52_out, and_53_out, and_54_out, and_55_out, and_56_out, and_57_out, and_58_out,
       and_75_out, and_76_out, and_77_out, and_78_out, and_79_out, and_80_out, and_81_out, and_82_out,
       and_99_out, and_100_out, and_101_out, and_102_out, and_103_out, and_104_out, and_105_out, and_106_out,
       bit_extender_3_out, bit_extender_4_out, bit_extender_5_out, bit_extender_6_out, bit_extender_7_out,
       bit_extender_8_out, bit_extender_9_out, bit_extender_10_out, bit_extender_11_out, bit_extender_12_out,
       bit_extender_13_out, bit_extender_14_out, bit_extender_15_out, bit_extender_16_out,
       bit_extender_17_out, bit_extender_18_out, bit_extender_19_out, bit_extender_20_out,
       bit_extender_21_out, bit_extender_22_out, bit_extender_23_out, bit_extender_24_out,
       bit_extender_25_out, bit_extender_26_out, bit_extender_27_out, bit_extender_28_out,
       bit_extender_29_out, bit_extender_30_out, bit_extender_31_out, bit_extender_32_out,
       bit_extender_33_out, bit_extender_34_out, bit_extender_35_out, bit_extender_36_out,
       bit_extender_37_out, bit_extender_38_out, bit_extender_39_out, bit_extender_40_out,
       bit_extender_41_out, bit_extender_42_out, bit_extender_43_out, bit_extender_44_out,
       bit_extender_45_out, multiplexer_1_out, multiplexer_4_out, multiplexer_6_out, multiplexer_7_out,
       multiplexer_8_out, multiplexer_9_out, multiplexer_11_out, nand_5_out, nand_9_out, or_1_out, or_3_out,
       or_4_out, or_5_out, or_6_out, or_7_out, or_8_out, or_9_out, or_10_out, or_11_out, or_12_out,
       or_13_out, or_14_out, or_15_out, or_16_out, or_17_out, or_18_out, or_19_out, or_20_out, or_21_out,
       or_22_out, or_23_out, or_24_out, or_25_out, or_26_out, or_27_out, or_28_out, or_29_out, or_30_out,
       or_31_out, or_32_out, or_33_out, PC_q, ram_1_dout, ram_2_dout, register_1_q, register_2_q,
       register_4_q, register_5_q, register_6_q, register_7_q, register_8_q, register_9_q, register_10_q,
       register_11_q, register_12_q, register_13_q, register_14_q, register_15_q, register_16_q,
       register_17_q, register_18_q, register_19_q, register_20_q, register_21_q, register_22_q,
       register_23_q, shifter_1_out, shifter_2_out, shifter_3_out, subtractor_1_out, xor_3_out;
  wire [23:0] and_2_out, and_3_out, bit_extender_1_out, bit_extender_2_out;
  wire [23:16] undriven, undriven_2;
  wire [31:0] multiplexer_10_out;
  wire [31:5] multiplexer_5_out_2;

  Clock clock_1 (.out(clock_1_out));
  RAM #(.addrWidth(24), .dataWidth(16), .trigger("high"), .databus("bibus")) ram_1 (
    .addr({undriven, PC_q}), .we(1'b0), .oe(1'b1), .dout(ram_1_dout));  // open: din
  RAM #(.addrWidth(24), .dataWidth(16), .trigger("falling"), .databus("bibus")) ram_2 (
    .addr(and_2_out), .we(and_1_out), .oe(1'b1), .clk(clock_1_out), .din(or_5_out), .dout(ram_2_dout));
  Comparator #(.width(6), .mode("unsigned")) comparator_1 (
    .a(multiplexer_10_out[5:0]), .b({6{1'b0}}), .eq(comparator_1_eq));  // open: gt, lt
  and and_1 (and_1_out, decoder_2_p6, comparator_1_eq);
  assign bit_extender_1_out = {{23{comparator_1_eq}}, comparator_1_eq};  // Bit_Extender bit_extender_1
  assign and_2_out = bit_extender_1_out & {undriven_2, multiplexer_10_out[15:0]};  // AND_Gate and_2, 24 bits wide
  Comparator #(.width(16)) comparator_2 (
    .a(or_4_out), .b(or_5_out), .eq(comparator_2_eq), .lt(comparator_2_lt));  // open: gt
  Comparator #(.width(16), .mode("unsigned")) comparator_3 (
    .a(or_4_out), .b(or_5_out), .eq(comparator_3_eq), .lt(comparator_3_lt));  // open: gt
  assign bit_extender_2_out = {{23{comparator_4_gt}}, comparator_4_gt};  // Bit_Extender bit_extender_2
  Comparator #(.width(6), .mode("unsigned")) comparator_4 (
    .a(multiplexer_10_out[31:26]), .b({6{1'b0}}), .gt(comparator_4_gt), .eq(comparator_4_gt),
    .lt(comparator_4_gt));
  Adder #(.width(16)) adder_1 (.a(PC_q), .b(16'h4), .out(adder_1_out));  // open: cin, cout
  Register #(.width(16)) PC (.D(multiplexer_1_out), .clk(clock_1_out), .Q(PC_q));  // open: en, clr
  Multiplexer #(.width(16), .enable("false")) multiplexer_1 (
    .in0(adder_1_out), .in1(multiplexer_10_out[15:0]), .out(multiplexer_1_out), .sel(nand_18_out));
  Multiplexer #(.enable("false")) multiplexer_2 (
    .in0(comparator_2_eq), .in1(comparator_3_eq), .out(multiplexer_2_out), .sel(ram_1_dout[7]));
  Multiplexer #(.enable("false")) multiplexer_3 (
    .in0(comparator_2_lt), .in1(comparator_3_lt), .out(multiplexer_3_out), .sel(ram_1_dout[7]));
  Decoder #(.select(3)) decoder_1 (
    .out0(decoder_1_out0), .out1(decoder_1_out1), .out2(decoder_1_out2), .out6(decoder_1_out6),
    .out7(decoder_1_out7), .en(and_4_out));  // open: out3, out4, out5, sel
  assign and_3_out = multiplexer_10_out[25:2] & bit_extender_2_out;  // AND_Gate and_3, 24 bits wide
  and and_4 (and_4_out, comparator_4_gt, decoder_2_p6);
  // Decoder #(.select(5), .enable("false")) decoder_2: pin names not known; wires that end beside it: {decoder_2_p1, ram_1_dout[2:0]}, {decoder_2_p1, ram_1_dout[2:0]}, decoder_2_p3[0], decoder_2_p4, decoder_2_p5, decoder_2_p6, decoder_2_p7, decoder_2_p8, decoder_2_p9, decoder_2_p10, decoder_2_p11
  Bit_Extender #(.in_width(16)) bit_extender_3 (.in(nand_5_out), .out(bit_extender_3_out));
  assign and_5_out = bit_extender_3_out & bit_extender_4_out;  // AND_Gate and_5, 16 bits wide
  Bit_Extender #(.in_width(16)) bit_extender_4 (.in(ram_1_dout), .out(bit_extender_4_out));
  assign bit_extender_5_out = {{15{decoder_2_p6}}, decoder_2_p6};  // Bit_Extender bit_extender_5
  assign and_6_out = bit_extender_5_out & bit_extender_6_out;  // AND_Gate and_6, 16 bits wide
  assign bit_extender_6_out = {{8{ram_1_dout[11]}}, {ram_1_dout[11:8], ram_1_dout[3:0]}};  // Bit_Extender bit_extender_6
  assign bit_extender_7_out = {{15{decoder_2_p9}}, decoder_2_p9};  // Bit_Extender bit_extender_7
  assign and_7_out = bit_extender_7_out & bit_extender_8_out;  // AND_Gate and_7, 16 bits wide
  assign bit_extender_8_out = {{4{undriven_9[1]}}, {undriven_9, undriven_8[9:8], undriven_8[5:4], undriven_8[2:0], undriven_7, 1'b0}};  // Bit_Extender bit_extender_8
  Bit_Extender #(.in_width(16)) bit_extender_9 (.in(nand_9_out), .out(bit_extender_9_out));
  assign and_8_out = bit_extender_9_out & {ram_1_dout[7:0], {8{1'b0}}};  // AND_Gate and_8, 16 bits wide
  assign bit_extender_10_out = {{15{decoder_2_p11}}, decoder_2_p11};  // Bit_Extender bit_extender_10
  assign and_9_out = bit_extender_10_out & bit_extender_11_out;  // AND_Gate and_9, 16 bits wide
  assign bit_extender_11_out = {{4{ram_1_dout[13]}}, {ram_1_dout[13:12], ram_1_dout[9:8], ram_1_dout[5:4], ram_1_dout[2:0], ram_1_dout[2:0]}};  // Bit_Extender bit_extender_11
  xor xor_1 (xor_1_out, ram_1_dout[6], multiplexer_2_out);
  xor xor_2 (xor_2_out, ram_1_dout[6], multiplexer_3_out);
  Register #(.width(16)) register_1 (
    .D(or_5_out), .en(decoder_1_out0), .clk(clock_1_out), .Q(register_1_q));  // open: clr
  Register #(.width(16)) register_2 (
    .D(or_5_out), .en(decoder_1_out7), .clk(clock_1_out), .Q(register_2_q));  // open: clr
  nand nand_1 (nand_1_out, decoder_2_p3[0], decoder_2_p3[0]);
  assign or_1_out = and_5_out | and_6_out | and_7_out | and_8_out | and_9_out;  // OR_Gate or_1, 16 bits wide
  and and_10 (and_10_out, ~ram_1_dout[8], xor_1_out);  // AND_Gate
  or or_2 (or_2_out, and_10_out, and_11_out);
  and and_11 (and_11_out, ram_1_dout[8], xor_2_out);
  nand nand_2 (nand_2_out, decoder_2_p10, decoder_2_p10);
  nand nand_3 (nand_3_out, nand_2_out, nand_6_out);
  nand nand_4 (nand_4_out, nand_3_out, nand_3_out);
  nand nand_5 (nand_5_out[0], nand_1_out, nand_4_out);
  Register #(.width(13)) register_3 (
    .D(or_5_out[12:0]), .en(decoder_1_out1), .clk(clock_1_out), .Q(register_3_q));  // open: clr
  Register #(.width(16)) register_4 (.D(or_5_out), .en(undriven_10), .clk(clock_1_out), .Q(register_4_q));  // open: clr
  nand nand_6 (nand_6_out, decoder_2_p4, decoder_2_p4);
  nand nand_7 (nand_7_out, decoder_2_p8, decoder_2_p8);
  nand nand_8 (nand_8_out, decoder_2_p5, decoder_2_p5);
  nand nand_9 (nand_9_out[0], nand_8_out, nand_7_out);
  Multiplexer #(.width(16), .enable("false")) multiplexer_4 (
    .in0(or_4_out), .in1(PC_q), .out(multiplexer_4_out), .sel(nand_20_out));
  Multiplexer #(.width(16), .enable("false")) multiplexer_5 (
    .in0(or_5_out), .in1(or_1_out), .out({multiplexer_5_out_2[15:5], multiplexer_5_out}), .sel(nand_22_out));
  Adder #(.width(16)) adder_2 (
    .a(multiplexer_4_out), .b({multiplexer_5_out_2[15:5], multiplexer_5_out}), .out(adder_2_out));  // open: cin, cout
  Subtractor #(.width(16)) subtractor_1 (
    .a(multiplexer_4_out), .b({multiplexer_5_out_2[15:5], multiplexer_5_out}), .out(subtractor_1_out));  // open: bin, bout
  Shifter #(.width(16)) shifter_1 (.in(multiplexer_4_out), .\dist (multiplexer_5_out[3:0]), .out(shifter_1_out));
  Comparator #(.width(16)) comparator_5 (
    .a(multiplexer_4_out), .b({multiplexer_5_out_2[15:5], multiplexer_5_out}), .lt(comparator_5_lt));  // open: gt, eq
  Comparator #(.width(16), .mode("unsigned")) comparator_6 (
    .a(multiplexer_4_out), .b({multiplexer_5_out_2[15:5], multiplexer_5_out}), .lt(comparator_6_lt));  // open: gt, eq
  assign xor_3_out = multiplexer_4_out ^ {multiplexer_5_out_2[15:5], multiplexer_5_out};  // XOR_Gate xor_3, 16 bits wide
  Shifter #(.width(16), .shift("lr")) shifter_2 (
    .in(multiplexer_4_out), .\dist (multiplexer_5_out[3:0]), .out(shifter_2_out));
  Shifter #(.width(16), .shift("ar")) shifter_3 (
    .in(multiplexer_4_out), .\dist (multiplexer_5_out[3:0]), .out(shifter_3_out));
  assign or_3_out = multiplexer_4_out | {multiplexer_5_out_2[15:5], multiplexer_5_out};  // OR_Gate or_3, 16 bits wide
  assign and_12_out = multiplexer_4_out & {multiplexer_5_out_2[15:5], multiplexer_5_out};  // AND_Gate and_12, 16 bits wide
  Register #(.width(16)) register_5 (
    .D(or_5_out), .en(decoder_1_out2), .clk(clock_1_out), .Q(register_5_q));  // open: clr
  Register #(.width(16)) register_6 (.D(or_5_out), .en(undriven_11), .clk(clock_1_out), .Q(register_6_q));  // open: clr
  nand nand_10 (nand_10_out, decoder_2_p11, decoder_2_p11);
  nand nand_11 (nand_11_out, decoder_2_p10, decoder_2_p10);
  nand nand_12 (nand_12_out, decoder_2_p9, or_2_out);
  nand nand_13 (nand_13_out, nand_11_out, nand_10_out);
  nand nand_14 (nand_14_out, nand_12_out, nand_12_out);
  nand nand_15 (nand_15_out, decoder_2_p11, decoder_2_p11);
  nand nand_16 (nand_16_out, nand_13_out, nand_13_out);
  nand nand_17 (nand_17_out, nand_14_out, nand_14_out);
  nand nand_18 (nand_18_out, nand_17_out, nand_16_out);
  Multiplexer #(.width(16), .enable("false")) multiplexer_6 (
    .in0(adder_2_out), .in1(subtractor_1_out), .out(multiplexer_6_out), .sel(undriven_4[0]));
  assign bit_extender_12_out = {{15{1'b0}}, comparator_5_lt};  // Bit_Extender bit_extender_12
  assign bit_extender_13_out = {{15{1'b0}}, comparator_6_lt};  // Bit_Extender bit_extender_13
  Multiplexer #(.width(16), .enable("false")) multiplexer_7 (
    .in0(shifter_2_out), .in1(shifter_3_out), .out(multiplexer_7_out), .sel(undriven_4[0]));
  nand nand_19 (nand_19_out, decoder_2_p9, decoder_2_p9);
  nand nand_20 (nand_20_out, nand_15_out, nand_19_out);
  nand nand_21 (nand_21_out, decoder_2_p4, decoder_2_p4);
  nand nand_22 (nand_22_out, decoder_2_p7, decoder_2_p7);
  Multiplexer #(.select(3), .width(16), .enable("false")) multiplexer_8 (
    .in0(multiplexer_6_out), .in1(shifter_1_out), .in2(bit_extender_12_out), .in3(bit_extender_13_out),
    .in4(xor_3_out), .in5(multiplexer_7_out), .in6(or_3_out), .in7(and_12_out), .out(multiplexer_8_out),
    .sel(ram_1_dout[8:6]));
  Register #(.width(16)) register_7 (
    .D(or_5_out), .en(decoder_1_out6), .clk(clock_1_out), .Q(register_7_q));  // open: clr
  Register #(.width(16)) register_8 (.D(or_5_out), .en(undriven_12), .clk(clock_1_out), .Q(register_8_q));  // open: clr
  nand nand_23 (nand_23_out, decoder_2_p9, decoder_2_p9);
  nand nand_24 (nand_24_out, decoder_2_p10, decoder_2_p10);
  nand nand_25 (nand_25_out, decoder_2_p11, decoder_2_p11);
  nand nand_26 (decoder_2_p3[1], nand_25_out, nand_24_out);
  nand nand_27 (nand_27_out, decoder_2_p7, decoder_2_p7);
  nand nand_28 (nand_28_out, nand_21_out, nand_27_out);
  Multiplexer #(.width(16), .enable("false")) multiplexer_9 (
    .in0(adder_2_out), .in1(multiplexer_8_out), .out(multiplexer_9_out), .sel(nand_28_out));
  Multiplexer #(.width(16), .enable("false")) multiplexer_10 (
    .in0(multiplexer_9_out), .in1({multiplexer_5_out_2[15:5], multiplexer_5_out}),
    .out(multiplexer_10_out[15:0]), .sel(decoder_2_p8));
  nand nand_29 (nand_29_out, decoder_2_p6, decoder_2_p6);
  nand nand_30 (nand_30_out, nand_23_out, nand_29_out);
  nand nand_31 (nand_31_out, nand_30_out, nand_30_out);
  Multiplexer #(.select(2), .width(16), .enable("false")) multiplexer_11 (
    .in0(multiplexer_10_out[15:0]), .in1(ram_2_dout), .in2(adder_1_out), .out(multiplexer_11_out),
    .sel(decoder_2_p3));  // open: in3
  and and_13 (and_13_out, ~ram_1_dout[9], ~ram_1_dout[10], ~undriven_5[3], ~undriven_5[4]);  // AND_Gate
  and and_14 (and_14_out, ~ram_1_dout[12], ~ram_1_dout[13], ~ram_1_dout[15], ~undriven_6[4]);  // AND_Gate
  and and_15 (and_15_out, nand_31_out, and_16_out);
  and and_16 (and_16_out, ~ram_1_dout[3], ram_1_dout[4], ~undriven_3[3], ~undriven_3[4]);  // AND_Gate
  and and_17 (and_17_out, ~ram_1_dout[9], ram_1_dout[10], ~undriven_5[3], ~undriven_5[4]);  // AND_Gate
  and and_18 (and_18_out, ~ram_1_dout[12], ram_1_dout[13], ~ram_1_dout[15], ~undriven_6[4]);  // AND_Gate
  and and_19 (and_19_out, nand_31_out, and_20_out);
  and and_20 (and_20_out, ram_1_dout[3], ram_1_dout[4], ~undriven_3[3], ~undriven_3[4]);  // AND_Gate
  and and_21 (and_21_out, ram_1_dout[9], ram_1_dout[10], ~undriven_5[3], ~undriven_5[4]);  // AND_Gate
  and and_22 (and_22_out, ram_1_dout[12], ram_1_dout[13], ~ram_1_dout[15], ~undriven_6[4]);  // AND_Gate
  and and_23 (and_23_out, nand_31_out, and_24_out);
  and and_24 (and_24_out, ram_1_dout[3], ram_1_dout[4], ~undriven_3[4]);  // AND_Gate
  and and_25 (and_25_out, ram_1_dout[9], ram_1_dout[10], ~undriven_5[4]);  // AND_Gate
  buf and_26 (and_26_out, ram_1_dout[12]);  // AND_Gate
  Register #(.width(16)) register_9 (.en(and_15_out), .clk(clock_1_out), .Q(register_9_q));  // open: D, clr
  Register #(.width(16)) register_10 (
    .D(multiplexer_11_out), .en(and_19_out), .clk(clock_1_out), .Q(register_10_q));  // open: clr
  Register #(.width(16)) register_11 (
    .D(multiplexer_11_out), .en(and_23_out), .clk(clock_1_out), .Q(register_11_q));  // open: clr
  assign or_4_out = or_12_out | or_6_out;  // OR_Gate or_4, 16 bits wide
  assign or_5_out = or_13_out | or_7_out;  // OR_Gate or_5, 16 bits wide
  assign and_27_out = {16{1'b0}} & bit_extender_14_out;  // AND_Gate and_27, 16 bits wide
  assign and_28_out = {16{1'b0}} & bit_extender_15_out;  // AND_Gate and_28, 16 bits wide
  assign bit_extender_14_out = {{15{and_13_out}}, and_13_out};  // Bit_Extender bit_extender_14
  assign bit_extender_15_out = {{15{and_14_out}}, and_14_out};  // Bit_Extender bit_extender_15
  assign and_29_out = register_9_q & bit_extender_16_out;  // AND_Gate and_29, 16 bits wide
  assign and_30_out = register_9_q & bit_extender_17_out;  // AND_Gate and_30, 16 bits wide
  assign bit_extender_16_out = {{15{and_17_out}}, and_17_out};  // Bit_Extender bit_extender_16
  assign bit_extender_17_out = {{15{and_18_out}}, and_18_out};  // Bit_Extender bit_extender_17
  assign and_31_out = register_10_q & bit_extender_18_out;  // AND_Gate and_31, 16 bits wide
  assign and_32_out = register_10_q & bit_extender_19_out;  // AND_Gate and_32, 16 bits wide
  assign bit_extender_18_out = {{15{and_21_out}}, and_21_out};  // Bit_Extender bit_extender_18
  assign bit_extender_19_out = {{15{and_22_out}}, and_22_out};  // Bit_Extender bit_extender_19
  assign and_33_out = register_11_q & bit_extender_20_out;  // AND_Gate and_33, 16 bits wide
  assign and_34_out = register_11_q & bit_extender_21_out;  // AND_Gate and_34, 16 bits wide
  assign bit_extender_20_out = {{15{and_25_out}}, and_25_out};  // Bit_Extender bit_extender_20
  assign bit_extender_21_out = {{15{and_26_out}}, and_26_out};  // Bit_Extender bit_extender_21
  assign or_6_out = and_27_out | or_8_out;  // OR_Gate or_6, 16 bits wide
  assign or_7_out = and_28_out | or_9_out;  // OR_Gate or_7, 16 bits wide
  assign or_8_out = and_29_out | or_10_out;  // OR_Gate or_8, 16 bits wide
  assign or_9_out = and_30_out | or_11_out;  // OR_Gate or_9, 16 bits wide
  assign or_10_out = and_31_out | and_33_out;  // OR_Gate or_10, 16 bits wide
  assign or_11_out = and_32_out | and_34_out;  // OR_Gate or_11, 16 bits wide
  and and_35 (and_35_out, ~ram_1_dout[3], ~ram_1_dout[4], ~undriven_3[3]);  // AND_Gate
  and and_36 (and_36_out, ~ram_1_dout[9], ~ram_1_dout[10], ~undriven_5[3]);  // AND_Gate
  and and_37 (and_37_out, ~ram_1_dout[12], ~ram_1_dout[13], ~ram_1_dout[15]);  // AND_Gate
  and and_38 (and_38_out, ~ram_1_dout[3], ram_1_dout[4], ~ram_1_dout[5], undriven_3[3], ~undriven_3[4]);  // AND_Gate
  and and_39 (and_39_out, ~ram_1_dout[9], ram_1_dout[10], ~ram_1_dout[11], undriven_5[3], ~undriven_5[4]);  // AND_Gate
  and and_40 (and_40_out, ~ram_1_dout[12], ram_1_dout[13], ~ram_1_dout[14], ram_1_dout[15], ~undriven_6[4]);  // AND_Gate
  and and_41 (and_41_out, ram_1_dout[3], ram_1_dout[4], ~ram_1_dout[5], undriven_3[3], ~undriven_3[4]);  // AND_Gate
  and and_42 (and_42_out, ram_1_dout[9], ram_1_dout[10], ~ram_1_dout[11], undriven_5[3], ~undriven_5[4]);  // AND_Gate
  and and_43 (and_43_out, ram_1_dout[12], ram_1_dout[13], ~ram_1_dout[14], ram_1_dout[15], ~undriven_6[4]);  // AND_Gate
  and and_44 (and_44_out, ram_1_dout[3], ram_1_dout[4], undriven_3[3]);
  and and_45 (and_45_out, ram_1_dout[9], ram_1_dout[10], undriven_5[3]);
  and and_46 (and_46_out, ram_1_dout[12], ram_1_dout[13], ram_1_dout[15]);
  Register #(.width(16)) register_12 (
    .D(multiplexer_11_out), .en(and_47_out), .clk(clock_1_out), .Q(register_12_q));  // open: clr
  and and_47 (and_47_out, nand_31_out, and_35_out);
  Register #(.width(16)) register_13 (
    .D(multiplexer_11_out), .en(and_48_out), .clk(clock_1_out), .Q(register_13_q));  // open: clr
  and and_48 (and_48_out, nand_31_out, and_38_out);
  Register #(.width(16)) register_14 (
    .D(multiplexer_11_out), .en(and_49_out), .clk(clock_1_out), .Q(register_14_q));  // open: clr
  and and_49 (and_49_out, nand_31_out, and_41_out);
  Register #(.width(16)) register_15 (
    .D(multiplexer_11_out), .en(and_50_out), .clk(clock_1_out), .Q(register_15_q));  // open: clr
  and and_50 (and_50_out, nand_31_out, and_44_out);
  assign or_12_out = or_20_out | or_14_out;  // OR_Gate or_12, 16 bits wide
  assign bit_extender_22_out = {{15{and_36_out}}, and_36_out};  // Bit_Extender bit_extender_22
  assign bit_extender_23_out = {{15{and_37_out}}, and_37_out};  // Bit_Extender bit_extender_23
  assign bit_extender_24_out = {{15{and_39_out}}, and_39_out};  // Bit_Extender bit_extender_24
  assign bit_extender_25_out = {{15{and_40_out}}, and_40_out};  // Bit_Extender bit_extender_25
  assign bit_extender_26_out = {{15{and_42_out}}, and_42_out};  // Bit_Extender bit_extender_26
  assign bit_extender_27_out = {{15{and_43_out}}, and_43_out};  // Bit_Extender bit_extender_27
  assign bit_extender_28_out = {{15{and_45_out}}, and_45_out};  // Bit_Extender bit_extender_28
  assign bit_extender_29_out = {{15{and_46_out}}, and_46_out};  // Bit_Extender bit_extender_29
  assign or_13_out = or_21_out | or_15_out;  // OR_Gate or_13, 16 bits wide
  assign or_14_out = and_51_out | or_16_out;  // OR_Gate or_14, 16 bits wide
  assign or_15_out = and_52_out | or_17_out;  // OR_Gate or_15, 16 bits wide
  assign and_51_out = register_12_q & bit_extender_22_out;  // AND_Gate and_51, 16 bits wide
  assign and_52_out = register_12_q & bit_extender_23_out;  // AND_Gate and_52, 16 bits wide
  assign or_16_out = and_53_out | or_18_out;  // OR_Gate or_16, 16 bits wide
  assign and_53_out = register_13_q & bit_extender_24_out;  // AND_Gate and_53, 16 bits wide
  assign or_17_out = or_18_out | or_19_out;  // OR_Gate or_17, 16 bits wide
  assign and_54_out = register_13_q & bit_extender_25_out;  // AND_Gate and_54, 16 bits wide
  assign or_18_out = and_55_out | and_57_out;  // OR_Gate or_18, 16 bits wide
  assign or_19_out = and_56_out | and_58_out;  // OR_Gate or_19, 16 bits wide
  assign and_55_out = register_14_q & bit_extender_26_out;  // AND_Gate and_55, 16 bits wide
  assign and_56_out = register_14_q & bit_extender_27_out;  // AND_Gate and_56, 16 bits wide
  assign and_57_out = register_15_q & bit_extender_28_out;  // AND_Gate and_57, 16 bits wide
  assign and_58_out = register_15_q & bit_extender_29_out;  // AND_Gate and_58, 16 bits wide
  and and_59 (and_59_out, nand_31_out, and_60_out);
  and and_60 (and_60_out, ~ram_1_dout[3], ~ram_1_dout[4], ~undriven_3[3], ~undriven_3[4]);  // AND_Gate
  and and_61 (and_61_out, ~ram_1_dout[9], ~ram_1_dout[10], ~undriven_5[3], ~undriven_5[4]);  // AND_Gate
  and and_62 (and_62_out, ~ram_1_dout[12], ~ram_1_dout[13], ~ram_1_dout[15], ~undriven_6[4]);  // AND_Gate
  and and_63 (and_63_out, nand_31_out, and_64_out);
  and and_64 (and_64_out, ~ram_1_dout[3], ram_1_dout[4], ~ram_1_dout[5], ~undriven_3[3], undriven_3[4]);  // AND_Gate
  and and_65 (and_65_out, ~ram_1_dout[9], ram_1_dout[10], ~ram_1_dout[11], ~undriven_5[3], undriven_5[4]);  // AND_Gate
  and and_66 (and_66_out, ~ram_1_dout[12], ram_1_dout[13], ~ram_1_dout[14], ~ram_1_dout[15], undriven_6[4]);  // AND_Gate
  and and_67 (and_67_out, nand_31_out, and_68_out);
  and and_68 (and_68_out, ram_1_dout[3], ram_1_dout[4], ~undriven_3[3], ~undriven_3[4]);  // AND_Gate
  and and_69 (and_69_out, ram_1_dout[9], ram_1_dout[10], ~undriven_5[3], ~undriven_5[4]);  // AND_Gate
  and and_70 (and_70_out, ram_1_dout[12], ram_1_dout[13], ~ram_1_dout[15], ~undriven_6[4]);  // AND_Gate
  and and_71 (and_71_out, nand_31_out, and_72_out);
  and and_72 (and_72_out, ram_1_dout[3], ram_1_dout[4], ~undriven_3[4]);  // AND_Gate
  and and_73 (and_73_out, ram_1_dout[9], ram_1_dout[10], ram_1_dout[11], ~undriven_5[3], undriven_5[4]);  // AND_Gate
  and and_74 (and_74_out, ram_1_dout[12], ram_1_dout[13], ram_1_dout[14], ~ram_1_dout[15], undriven_6[4]);  // AND_Gate
  assign or_20_out = or_28_out | or_22_out;  // OR_Gate or_20, 16 bits wide
  Register #(.width(16)) register_16 (
    .D(multiplexer_11_out), .en(and_59_out), .clk(clock_1_out), .Q(register_16_q));  // open: clr
  assign bit_extender_30_out = {{15{and_61_out}}, and_61_out};  // Bit_Extender bit_extender_30
  assign bit_extender_31_out = {{15{and_62_out}}, and_62_out};  // Bit_Extender bit_extender_31
  Register #(.width(16)) register_17 (
    .D(multiplexer_11_out), .en(and_63_out), .clk(clock_1_out), .Q(register_17_q));  // open: clr
  assign bit_extender_32_out = {{15{and_65_out}}, and_65_out};  // Bit_Extender bit_extender_32
  assign bit_extender_33_out = {{15{and_66_out}}, and_66_out};  // Bit_Extender bit_extender_33
  Register #(.width(16)) register_18 (
    .D(multiplexer_11_out), .en(and_67_out), .clk(clock_1_out), .Q(register_18_q));  // open: clr
  assign bit_extender_34_out = {{15{and_69_out}}, and_69_out};  // Bit_Extender bit_extender_34
  assign bit_extender_35_out = {{15{and_70_out}}, and_70_out};  // Bit_Extender bit_extender_35
  Register #(.width(16)) register_19 (
    .D(multiplexer_11_out), .en(and_71_out), .clk(clock_1_out), .Q(register_19_q));  // open: clr
  assign bit_extender_36_out = {{15{and_73_out}}, and_73_out};  // Bit_Extender bit_extender_36
  assign bit_extender_37_out = {{15{and_74_out}}, and_74_out};  // Bit_Extender bit_extender_37
  assign or_21_out = or_29_out | or_25_out;  // OR_Gate or_21, 16 bits wide
  assign or_22_out = and_75_out | or_23_out;  // OR_Gate or_22, 16 bits wide
  assign and_75_out = register_16_q & bit_extender_30_out;  // AND_Gate and_75, 16 bits wide
  assign and_76_out = register_16_q & bit_extender_31_out;  // AND_Gate and_76, 16 bits wide
  assign or_23_out = and_77_out | or_24_out;  // OR_Gate or_23, 16 bits wide
  assign and_77_out = register_17_q & bit_extender_32_out;  // AND_Gate and_77, 16 bits wide
  assign and_78_out = register_17_q & bit_extender_33_out;  // AND_Gate and_78, 16 bits wide
  assign or_24_out = and_79_out | and_81_out;  // OR_Gate or_24, 16 bits wide
  assign and_79_out = register_18_q & bit_extender_34_out;  // AND_Gate and_79, 16 bits wide
  assign and_80_out = register_18_q & bit_extender_35_out;  // AND_Gate and_80, 16 bits wide
  assign and_81_out = register_19_q & bit_extender_36_out;  // AND_Gate and_81, 16 bits wide
  assign and_82_out = register_19_q & bit_extender_37_out;  // AND_Gate and_82, 16 bits wide
  assign or_25_out = and_76_out | or_26_out;  // OR_Gate or_25, 16 bits wide
  assign or_26_out = and_78_out | or_27_out;  // OR_Gate or_26, 16 bits wide
  assign or_27_out = and_80_out | and_82_out;  // OR_Gate or_27, 16 bits wide
  and and_83 (and_83_out, ~ram_1_dout[3], ~ram_1_dout[4], ~undriven_3[3], undriven_3[4]);  // AND_Gate
  and and_84 (and_84_out, ~ram_1_dout[9], ~ram_1_dout[10], ~undriven_5[3], undriven_5[4]);  // AND_Gate
  and and_85 (and_85_out, ~ram_1_dout[12], ~ram_1_dout[13], ~ram_1_dout[15], undriven_6[4]);  // AND_Gate
  and and_86 (and_86_out, ~ram_1_dout[3], ram_1_dout[4], ~ram_1_dout[5], undriven_3[3], undriven_3[4]);  // AND_Gate
  and and_87 (and_87_out, ~ram_1_dout[9], ram_1_dout[10], ~ram_1_dout[11], undriven_5[3], undriven_5[4]);  // AND_Gate
  and and_88 (and_88_out, ~ram_1_dout[12], ram_1_dout[13], ~ram_1_dout[14], ram_1_dout[15], undriven_6[4]);  // AND_Gate
  and and_89 (and_89_out, ram_1_dout[3], ram_1_dout[4], ~undriven_3[3], undriven_3[4]);  // AND_Gate
  and and_90 (and_90_out, ram_1_dout[9], ram_1_dout[10], ~undriven_5[3], undriven_5[4]);  // AND_Gate
  and and_91 (and_91_out, ram_1_dout[12], ram_1_dout[13], ~ram_1_dout[15], undriven_6[4]);  // AND_Gate
  and and_92 (and_92_out, ram_1_dout[3], ram_1_dout[4], undriven_3[3], undriven_3[4]);
  and and_93 (and_93_out, ram_1_dout[9], ram_1_dout[10], undriven_5[3], undriven_5[4]);
  and and_94 (and_94_out, ram_1_dout[12], ram_1_dout[13], ram_1_dout[15], undriven_6[4]);
  Register #(.width(16)) register_20 (
    .D(multiplexer_11_out), .en(and_95_out), .clk(clock_1_out), .Q(register_20_q));  // open: clr
  and and_95 (and_95_out, nand_31_out, and_83_out);
  Register #(.width(16)) register_21 (
    .D(multiplexer_11_out), .en(and_96_out), .clk(clock_1_out), .Q(register_21_q));  // open: clr
  and and_96 (and_96_out, nand_31_out, and_86_out);
  Register #(.width(16)) register_22 (
    .D(multiplexer_11_out), .en(and_97_out), .clk(clock_1_out), .Q(register_22_q));  // open: clr
  and and_97 (and_97_out, nand_31_out, and_89_out);
  Register #(.width(16)) register_23 (
    .D(multiplexer_11_out), .en(and_98_out), .clk(clock_1_out), .Q(register_23_q));  // open: clr
  and and_98 (and_98_out, nand_31_out, and_92_out);
  assign bit_extender_38_out = {{15{and_84_out}}, and_84_out};  // Bit_Extender bit_extender_38
  assign bit_extender_39_out = {{15{and_85_out}}, and_85_out};  // Bit_Extender bit_extender_39
  assign bit_extender_40_out = {{15{and_87_out}}, and_87_out};  // Bit_Extender bit_extender_40
  assign bit_extender_41_out = {{15{and_88_out}}, and_88_out};  // Bit_Extender bit_extender_41
  assign bit_extender_42_out = {{15{and_90_out}}, and_90_out};  // Bit_Extender bit_extender_42
  assign bit_extender_43_out = {{15{and_91_out}}, and_91_out};  // Bit_Extender bit_extender_43
  assign bit_extender_44_out = {{15{and_93_out}}, and_93_out};  // Bit_Extender bit_extender_44
  assign bit_extender_45_out = {{15{and_94_out}}, and_94_out};  // Bit_Extender bit_extender_45
  assign or_28_out = and_99_out | or_30_out;  // OR_Gate or_28, 16 bits wide
  assign or_29_out = and_100_out | or_31_out;  // OR_Gate or_29, 16 bits wide
  assign and_99_out = register_20_q & bit_extender_38_out;  // AND_Gate and_99, 16 bits wide
  assign and_100_out = register_20_q & bit_extender_39_out;  // AND_Gate and_100, 16 bits wide
  assign or_30_out = and_101_out | or_32_out;  // OR_Gate or_30, 16 bits wide
  assign or_31_out = and_102_out | or_33_out;  // OR_Gate or_31, 16 bits wide
  assign and_101_out = register_21_q & bit_extender_40_out;  // AND_Gate and_101, 16 bits wide
  assign and_102_out = register_21_q & bit_extender_41_out;  // AND_Gate and_102, 16 bits wide
  assign or_32_out = and_103_out | and_105_out;  // OR_Gate or_32, 16 bits wide
  assign or_33_out = and_104_out | and_106_out;  // OR_Gate or_33, 16 bits wide
  assign and_103_out = register_22_q & bit_extender_42_out;  // AND_Gate and_103, 16 bits wide
  assign and_104_out = register_22_q & bit_extender_43_out;  // AND_Gate and_104, 16 bits wide
  assign and_105_out = register_23_q & bit_extender_44_out;  // AND_Gate and_105, 16 bits wide
  assign and_106_out = register_23_q & bit_extender_45_out;  // AND_Gate and_106, 16 bits wide
  TTY tty_1 (.data(ram_2_dout[6:0]), .clk(clock_1_out));  // open: we, clr
  DotMatrix #(.inputtype("row"), .matrixcols(8), .matrixrows(8)) dotmatrix_1 (
    .row0(register_1_q[7:0]), .row1(register_3_q[7:0]), .row2(register_5_q[7:0]), .row3(register_7_q[7:0]),
    .row4(register_2_q[7:0]), .row5(register_4_q[7:0]), .row6(register_6_q[7:0]), .row7(register_8_q[7:0]));
  // Pins of 16 and 32 bits meet at {multiplexer_5_out_2, multiplexer_5_out}
  // Pins of 4 and 5 bits meet at multiplexer_5_out
  // Pins of 4 and 5 bits meet at multiplexer_5_out
  // Pins of 4 and 16 bits meet at {multiplexer_5_out_2[15:5], multiplexer_5_out}
  // Pins of 1 and 6 bits meet at undriven_4
  // Pins of 13 and 16 bits meet at or_5_out
  // Pins of 1 and 3 bits meet at {undriven_7, 1'b0}
  // Pins of 16 and 32 bits meet at multiplexer_10_out
  // Pins of 1 and 3 and 4 bits meet at ram_1_dout[3:0]
  // Pins of 2 and 4 bits meet at ram_1_dout[7:4]
  // Pins of 2 and 4 bits meet at ram_1_dout[11:8]
  // Pins of 2 and 4 bits meet at ram_1_dout[15:12]
  // also tied to GND on the sheet: ram_1_dout[0]

  // Notes on the sheet:
  //   Branch Comp
  //   I/O
  //   load
  //   auipc
  //   store
  //   ALU_imm
  //   ALU_reg
  //   lui
  //   branch
  //   jalr
  //   jal
  //   Imm Gen
  //   Control Logic
  //   AND
  //   3 INPUT OR
  //   ALU
  //   OR
  //   OR
  //   NOR 
  //   rsA
  //   rsB
  //   Reg File
endmodule
